// Logisim project trabalho_final.circ as structural Verilog: 1 circuit, main circuit main
module main (
  input  [7:0] B,
  input  [7:0] A,
  input  in_3,
  input  [1:0] in_4,
  input  [1:0] in_5,
  input  [1:0] in_6,
  output [7:0] out_7,
  output [7:0] out_8
);

  wire clock_1_out, demultiplexer_1_out0, demultiplexer_1_out1, demultiplexer_1_out2, demultiplexer_1_out3;
  wire [7:0] multiplexer_1_out, register_1_q, register_2_q, register_3_q, register_4_q;

  Clock clock_1 (.out(clock_1_out));
  Demultiplexer #(.select(2)) demultiplexer_1 (
    .out0(demultiplexer_1_out0), .out1(demultiplexer_1_out1), .out2(demultiplexer_1_out2),
    .out3(demultiplexer_1_out3), .in(clock_1_out), .sel(in_6));
  Multiplexer #(.width(8)) multiplexer_1 (.in0(A), .in1(B), .out(multiplexer_1_out), .sel(in_3));
  Register register_1 (.D(multiplexer_1_out), .clk(demultiplexer_1_out0), .Q(register_1_q));  // open: en, clr
  Register register_2 (.D(multiplexer_1_out), .clk(demultiplexer_1_out1), .Q(register_2_q));  // open: en, clr
  Multiplexer #(.select(2), .width(8)) multiplexer_2 (
    .in0(register_1_q), .in1(register_2_q), .in2(register_3_q), .in3(register_4_q), .out(out_7), .sel(in_4));
  Register register_3 (.D(multiplexer_1_out), .clk(demultiplexer_1_out2), .Q(register_3_q));  // open: en, clr
  Register register_4 (.D(multiplexer_1_out), .clk(demultiplexer_1_out3), .Q(register_4_q));  // open: en, clr
  Multiplexer #(.select(2), .width(8)) multiplexer_3 (
    .in0(register_1_q), .in1(register_2_q), .in2(register_3_q), .in3(register_4_q), .out(out_8), .sel(in_5));
endmodule
